# Fritzing sketch ckt (saved by Fritzing 0.9.3b)

parts:
  MPX4250AP1 = MPX4250AP pressure sensor [part_number=MPX]
  Part1 = Arduino Nano (Rev3.0)
  SEN1 = Pulse Sensor [package=SIP-3]
  Part2 = HC-05 [part_number=HC-05 package="breakout board"]
  Grove1 = Grove OLED 128x96

nets:
  N1: MPX4250AP1.V_out, Part1.A0
  GND: MPX4250AP1.GND, Part1.GND, SEN1.GND, Part2.GND, Grove1.GND
  VCC: MPX4250AP1.Vs, Part1.5V, SEN1.VCC, Part2.VCC, Grove1.VCC
  N2: Part1.D1/TX, Part2.TXD
  N3: Part1.D0/RX, Part2.RXD
  N4: Part1.A5, Grove1.SCL
  N5: Part1.A4, Grove1.SDA
  N6: Part1.A1, SEN1.Signal

custom parts:
  Pulse Sensor: Pulse Sensor Optical Heart Beat Sensor
  HC-05: A commonly available HC-05 Bluetooth breakout board.
